# Fritzing sketch VA219 (saved by Fritzing 0.9.2b)
breadboards: 1

parts:
  パーツ1 = PowerBoost 500 Charger
  パーツ2 = Pro Trinket 3.3V  # not connected
  7SEG1 = 7-Segment LED I2C Backpack (red)  # not connected
  7SEG2 = 7-Segment LED I2C Backpack (blue)  # not connected
  U1 = MAX7219 [package=dil24]  # not connected
  INA1 = INA219 DC Current Sensor Breakout
  パーツ3 = Arduino Pro Mini v13

nets:
  GND: パーツ1.GND, INA1.GND, パーツ3.GND
  N1: パーツ1.5.0V, パーツ3.RAW
  VCC: INA1.VCC, パーツ3.VCC
  N2: INA1.SCL, パーツ3.A5
  N3: INA1.SDA, パーツ3.A4

custom parts:
  PowerBoost 500 Charger: The PowerBoost 500C is a little DC/DC boost converter module that can be powered by any 3.7V LiIon/LiPoly battery, and convert the battery output to 5.2V DC for running your 5V projects. At its heart is a TPS61090 boost converter from TI. This boost converter chip has some really nice extras such as low battery detection, 2A internal switch, synchronous conversion, excellent efficiency, and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
  Pro Trinket 3.3V: The Pro Trinket 3.3V is like an Arduino Pro Mini with more pins and USB included. However, it uses 3V logic and 12MHz clock which means it's good when you want a lower-power and lower-voltage setup. Built with the common core Arduino chip, the ATmega328p, it has 18 GPIO, 2 extra analog inputs, 28K of flash, and 2K of RAM. It has onboard USB bootloading support with Optiboot support, so you can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
  7-Segment LED I2C Backpack (red): 4-digit, 7-segment LED Display with I2C Control
  7-Segment LED I2C Backpack (blue): 4-digit, 7-segment LED Display with I2C Control
  INA219 DC Current Sensor Breakout: INA DC Current Sensor Breakout
